# Fritzing sketch Hardware (saved by Fritzing 0.9.3b)
breadboards: 1

parts:
  Arduino_Uno = Arduino Uno (Rev3)
  U2 = 74HC595 [package="DIP16 [THT]"]
  R10 = Resistor [tolerance=±5% resistance=220 package=THT]
  R11 = Resistor [tolerance=±5% resistance=220 package=THT]
  R12 = Resistor [tolerance=±5% resistance=220 package=THT]
  R13 = Resistor [tolerance=±5% resistance=220 package=THT]
  R14 = Resistor [tolerance=±5% resistance=220 package=THT]
  R15 = Resistor [tolerance=±5% resistance=220 package=THT]
  R16 = Resistor [tolerance=±5% resistance=220 package=THT]
  Buzzer = Piezo Speaker
  R17 = Resistor [tolerance=±5% resistance=220 package=THT]
  LED1 = LED - 5mm [color="Red (633nm)" package="5 mm [THT]"]
  LED2 = LED - 5mm [color="Yellow (592nm)" package="5 mm [THT]"]
  LED3 = LED - 5mm [color="Green (560nm)" package="5 mm [THT]"]
  LED4 = LED - 5mm [color="Green (565nm)" package="5 mm [THT]"]
  LED5 = LED - 5mm [color="Yellow (592nm)" package="5 mm [THT]"]
  LED6 = LED - 5mm [color="Red (633nm)" package="5 mm [THT]"]
  R18 = Resistor [tolerance=±5% resistance=220 package=THT]
  R19 = Resistor [tolerance=±5% resistance=220 package=THT]
  R20 = Resistor [tolerance=±5% resistance=220 package=THT]
  R21 = Resistor [tolerance=±5% resistance=220 package=THT]
  R22 = Resistor [tolerance=±5% resistance=220 package=THT]
  R23 = Resistor [tolerance=±5% resistance=220 package=THT]
  J1 = Basic Servo
  C1 = Electrolytic Capacitor [capacitance=10µF voltage=10V package="100 mil [THT, electrolytic]"]
  R25 = Resistor [tolerance=±5% resistance=10k package=THT]
  S1 = Pushbutton [package="[THT]"]
  R26 = Resistor [tolerance=±5% resistance=10k package=THT]
  S2 = Pushbutton [package="[THT]"]
  R27 = Resistor [tolerance=±5% resistance=10k package=THT]
  S3 = Pushbutton [package="[THT]"]
  R28 = Resistor [tolerance=±5% resistance=10k package=THT]
  S4 = Pushbutton [package="[THT]"]
  R29 = Photocell (LDR) [package=THT]
  R30 = Resistor [tolerance=±5% resistance=10k package=THT]
  7_Segment1 = 7 Segment Display

nets:
  5V: Arduino_Uno.A0, Arduino_Uno.A1, Arduino_Uno.5V, U2.MR, U2.VCC, R25.Pin_0, S1.Pin_3, S1.Pin_4, R26.Pin_0, S2.Pin_3, S2.Pin_4
  N1: Arduino_Uno.A2, Arduino_Uno.A3, R27.Pin_0, S3.Pin_3, S3.Pin_4, R28.Pin_0, S4.Pin_3, S4.Pin_4, R29.pin_0
  N2: Arduino_Uno.A4/SDA, R29.pin_1, R30.Pin_0
  N3: Arduino_Uno.D8, R22.Pin_1
  N4: Arduino_Uno.D9_PWM, R21.Pin_1
  N5: Arduino_Uno.D10_PWM/SS, U2.SH_CP
  N6: Arduino_Uno.D11_PWM/MOSI, U2.ST_CP
  N7: Arduino_Uno.D12/MISO, U2.DS
  N8: Arduino_Uno.D13/SCK, Buzzer.pin2
  GND: Arduino_Uno.GND, U2.GND, U2.OE, R17.Pin_0, LED4.cathode, LED5.cathode, LED6.cathode, R25.Pin_1, R26.Pin_1, R27.Pin_1, R28.Pin_1, R30.Pin_1, 7_Segment1.common_anode
  N9: Arduino_Uno.D3_PWM, J1.pulse
  N10: Arduino_Uno.D4, R18.Pin_1
  N11: Arduino_Uno.D5_PWM, R19.Pin_1
  N12: Arduino_Uno.D6_PWM, R20.Pin_1
  N13: Arduino_Uno.D7, R23.Pin_1
  N14: U2.Q1, R15.Pin_1
  N15: U2.Q2, R14.Pin_1
  N16: U2.Q3, R13.Pin_1
  N17: U2.Q4, R12.Pin_1
  N18: U2.Q5, R11.Pin_1
  N19: U2.Q6, R10.Pin_1
  N20: U2.Q0, R16.Pin_1
  N21: R10.Pin_0, 7_Segment1.Segment_G
  N22: R11.Pin_0, 7_Segment1.Segment_F
  N23: R12.Pin_0, 7_Segment1.Segment_E
  N24: R13.Pin_0, 7_Segment1.Segment_D
  N25: R14.Pin_0, 7_Segment1.Segment_C
  N26: R15.Pin_0, 7_Segment1.Segment_B
  N27: R16.Pin_0, 7_Segment1.Segment_A
  N28: Buzzer.pin1, R17.Pin_1
  N29: LED1.cathode, LED2.cathode, LED3.cathode, J1.gnd, C1.-
  N30: LED1.anode, R21.Pin_0
  N31: LED2.anode, R22.Pin_0
  N32: LED3.anode, R23.Pin_0
  N33: LED4.anode, R20.Pin_0
  N34: LED5.anode, R19.Pin_0
  N35: LED6.anode, R18.Pin_0
  N36: J1.vcc, C1.+

notes:
  halve cirkel links
