# Fritzing sketch Hardware_Breadboard (saved by Fritzing 0.9.3b)
breadboards: 1

parts:
  Onderdeel1 = Arduino Uno (Rev3)
  S1 = Pushbutton [package="[THT]"]
  R1 = Photocell (LDR) [package=THT]
  R2 = Resistor [tolerance=±5% resistance=10k package=THT]
  R3 = Resistor [tolerance=±5% resistance=10k package=THT]
  LED1 = LED - 5mm [color="Green (565nm)" package="5 mm [THT]"]
  LED2 = LED - 5mm [color="Orange (612nm)" package="5 mm [THT]"]
  LED3 = LED - 5mm [color="Red (633nm)" package="5 mm [THT]"]
  R4 = Resistor [tolerance=±5% resistance=220 package=THT]
  R5 = Resistor [tolerance=±5% resistance=220 package=THT]
  R6 = Resistor [tolerance=±5% resistance=220 package=THT]
  S2 = Pushbutton [package="[THT]"]
  R7 = Resistor [tolerance=±5% resistance=10k package=THT]
  J1 = Piezo Speaker
  R8 = Resistor [tolerance=±5% resistance=220 package=THT]
  C1 = Electrolytic Capacitor [capacitance=1µF package="100 mil [THT, electrolytic]"]
  J2 = Basic Servo
  U1 = 74HC595 [package="DIP16 [THT]"]
  7_Segment1 = 7 Segment Display
  R9 = Resistor [tolerance=±5% resistance=220 package=THT]
  R10 = Resistor [tolerance=±5% resistance=220 package=THT]
  R11 = Resistor [tolerance=±5% resistance=220 package=THT]
  R12 = Resistor [tolerance=±5% resistance=220 package=THT]
  R13 = Resistor [tolerance=±5% resistance=220 package=THT]
  R15 = Resistor [tolerance=±5% resistance=220 package=THT]
  R16 = Resistor [tolerance=±5% resistance=220 package=THT]
  S3 = Pushbutton [package="[THT]"]
  S4 = Pushbutton [package="[THT]"]
  R17 = Resistor [tolerance=±5% resistance=220 package=THT]
  R18 = Resistor [tolerance=±5% resistance=220 package=THT]
  R19 = Resistor [tolerance=±5% resistance=220 package=THT]
  R20 = Resistor [tolerance=±5% resistance=10k package=THT]
  R21 = Resistor [tolerance=±5% resistance=10k package=THT]
  LED4 = LED - 5mm [color="Red (633nm)" package="5 mm [THT]"]
  LED5 = LED - 5mm [color="Orange (612nm)" package="5 mm [THT]"]
  LED6 = LED - 5mm [color="Green (565nm)" package="5 mm [THT]"]

nets:
  N1: Onderdeel1.A0, S1.Pin_1, S1.Pin_2, R3.Pin_0
  N2: Onderdeel1.A1, S4.Pin_3, S4.Pin_4, R20.Pin_1
  N3: Onderdeel1.A2, S3.Pin_3, S3.Pin_4, R21.Pin_1
  N4: Onderdeel1.A3, S2.Pin_1, S2.Pin_2, R7.Pin_0
  N5: Onderdeel1.A4/SDA, R1.pin_1, R2.Pin_0
  N6: Onderdeel1.D8, LED5.cathode
  N7: Onderdeel1.D9_PWM, LED4.cathode
  N8: Onderdeel1.D10_PWM/SS, U1.MR
  N9: Onderdeel1.D11_PWM/MOSI, U1.SH_CP
  N10: Onderdeel1.D12/MISO, U1.OE
  N11: Onderdeel1.D13/SCK, J1.pin2
  GND: Onderdeel1.GND, R2.Pin_1, R3.Pin_1, R4.Pin_1, R5.Pin_1, R6.Pin_1, R7.Pin_1, R8.Pin_1, C1.-, J2.gnd, U1.GND, U1.ST_CP, R17.Pin_0, R19.Pin_0, R20.Pin_0
  N12: Onderdeel1.D3_PWM, J2.pulse
  N13: Onderdeel1.D4, LED1.anode
  N14: Onderdeel1.D5_PWM, LED2.cathode
  N15: Onderdeel1.D6_PWM, LED3.cathode
  N16: Onderdeel1.D7, LED6.cathode
  VCC: S1.Pin_3, S1.Pin_4, R1.pin_0, S2.Pin_3, S2.Pin_4, C1.+, J2.vcc, U1.VCC, S3.Pin_1, S3.Pin_2, S4.Pin_1, S4.Pin_2, R21.Pin_0
  N17: LED1.cathode, R4.Pin_0
  N18: LED2.anode, R5.Pin_0
  N19: LED3.anode, R6.Pin_0
  N20: J1.pin1, R8.Pin_0
  N21: U1.Q1, R11.Pin_0
  N22: U1.Q2, R13.Pin_0
  N23: U1.Q3, R16.Pin_1
  N24: U1.Q4, R15.Pin_1
  N25: U1.Q5, R10.Pin_1
  N26: U1.Q6, R9.Pin_1
  N27: U1.Q0, R12.Pin_0
  N28: 7_Segment1.Segment_D, R13.Pin_1
  N29: 7_Segment1.Segment_C, R15.Pin_0
  N30: 7_Segment1.Segment_DP, R16.Pin_0
  N31: 7_Segment1.Segment_B, R9.Pin_0
  N32: 7_Segment1.Segment_A, R10.Pin_0
  N33: 7_Segment1.Segment_F, R11.Pin_1
  N34: 7_Segment1.Segment_G, R12.Pin_1
  N35: R17.Pin_1, LED5.anode
  N36: R18.Pin_1, LED4.anode
  N37: R19.Pin_1, LED6.anode

notes:
  halve cirkel links
